# Fritzing sketch CPE301_FinalProject_Receiver (saved by Fritzing 0.9.3b)
breadboards: 1

parts:
  Part5 = NRF24L01+ Breakout Board
  Part6 = Arduino Mega 2560 (Rev3)
  3_3V = Battery Holders [package=battery]

nets:
  GND: Part5.GND, Part6.GND, 3_3V.-
  N1: Part5.VCC, 3_3V.+
  N2: Part5.CE, Part6.D53
  N3: Part5.CS, Part6.D48
  N4: Part5.SCK, Part6.D52
  N5: Part5.MOSI, Part6.D51
  N6: Part5.MISO, Part6.D50
